// Logisim project Control-Unit.circ as structural Verilog: 3 circuits, main circuit main
module main (
  input  [31:0] Instruction,
  output RegWrite,
  output RegDst,
  output ALUSrc,
  output Branch,
  output Memwrite,
  output MemtoReg,
  output [3:0] ALUOp,
  output Jump
);

  wire [6:0] multiplexer_1_out, multiplexer_2_out;

  ALU_Control alu_control_1 (.in_1(Instruction), .out_2(ALUOp));
  Multiplexer #(.select(5), .width(7), .disabled(0), .enable("false")) multiplexer_1 (
    .in0(7'b1100000), .in1(7'b0001000), .in2(7'b0010001), .in3(7'b0010001), .in4(7'b0001000),
    .in5(7'b0001000), .in6(7'b1010000), .in7(7'b1010000), .in8(7'b1010000), .in9(7'b1010000),
    .in10(7'b1010000), .in11(7'b1010000), .in12({7{1'b0}}), .in13({7{1'b0}}), .in14({7{1'b0}}),
    .in15(7'b1010000), .in16({7{1'b0}}), .in17({7{1'b0}}), .in18({7{1'b0}}), .in19({7{1'b0}}),
    .in20({7{1'b0}}), .in21({7{1'b0}}), .in22({7{1'b0}}), .in23({7{1'b0}}), .in24({7{1'b0}}),
    .in25({7{1'b0}}), .in26({7{1'b0}}), .in27({7{1'b0}}), .in28({7{1'b0}}), .in29({7{1'b0}}),
    .in30({7{1'b0}}), .in31({7{1'b0}}), .out(multiplexer_1_out), .sel(Instruction[30:26]));
  Multiplexer #(.select(5), .width(7), .enable("false")) multiplexer_2 (
    .in0({7{1'b0}}), .in1({7{1'b0}}), .in2({7{1'b0}}), .in3(7'b1010010), .in4({7{1'b0}}), .in5({7{1'b0}}),
    .in6({7{1'b0}}), .in7({7{1'b0}}), .in8({7{1'b0}}), .in9({7{1'b0}}), .in10({7{1'b0}}), .in11(7'b0010100),
    .in12({7{1'b0}}), .in13({7{1'b0}}), .in14({7{1'b0}}), .in15({7{1'b0}}), .in16({7{1'b0}}),
    .in17({7{1'b0}}), .in18({7{1'b0}}), .in19({7{1'b0}}), .in20({7{1'b0}}), .in21({7{1'b0}}),
    .in22({7{1'b0}}), .in23({7{1'b0}}), .in24({7{1'b0}}), .in25({7{1'b0}}), .in26({7{1'b0}}),
    .in27({7{1'b0}}), .in28({7{1'b0}}), .in29({7{1'b0}}), .in30({7{1'b0}}), .in31({7{1'b0}}),
    .out(multiplexer_2_out), .sel(Instruction[30:26]));
  Multiplexer #(.width(7), .enable("false")) multiplexer_3 (
    .in0(multiplexer_1_out), .in1(multiplexer_2_out),
    .out({RegWrite, RegDst, ALUSrc, Branch, Memwrite, MemtoReg, Jump}), .sel(Instruction[31]));

  // Other names for the same wires on the sheet: JP = Jump; MR = MemtoReg; MW = Memwrite; BR = Branch; AS = ALUSrc;
  //   RD = RegDst; RW = RegWrite; ALUS[3:0] = ALUOp; _5B[4:0] = Instruction[30:26]; _1B = Instruction[31]
endmodule

module ALU_Control (
  input  [31:0] in_1,
  output [3:0] out_2
);

  wire comparator_1_eq, Type_Control;
  wire [3:0] funct_decider_1_out_2, multiplexer_1_out, multiplexer_2_out, multiplexer_3_out;

  Funct_Decider funct_decider_1 (.in_1(in_1[5:0]), .out_2(funct_decider_1_out_2));
  Comparator #(.width(6)) comparator_1 (
    .a({6{1'b0}}), .b({in_1[30:26], in_1[31]}), .eq(comparator_1_eq));  // open: gt, lt
  not not_1 (Type_Control, comparator_1_eq);
  Multiplexer #(.select(5), .width(4), .enable("false")) multiplexer_1 (
    .in1(4'b0111), .in2(4'b0101), .in3(4'b0011), .in4(4'b0111), .in5(4'b0111), .in6(4'b0000), .in7(4'b0000),
    .in8(4'b0011), .in9(4'b0101), .in10(4'b1011), .in11(4'b1100), .in12(4'b1000), .in13(4'b1001),
    .in15(4'b0101), .in16(4'b0000), .in17(4'b0000), .in18(4'b0000), .in19(4'b0000), .in20(4'b0000),
    .in21(4'b0000), .in22(4'b0000), .in23(4'b0000), .in24(4'b0000), .in25(4'b0000), .in26(4'b0000),
    .in27(4'b0000), .in28(4'b0000), .in29(4'b0000), .in30(4'b0000), .in31(4'b0000), .out(multiplexer_1_out),
    .sel(in_1[30:26]));  // open: in0, in14
  Multiplexer #(.select(5), .width(4), .enable("false")) multiplexer_2 (
    .in0(4'b0000), .in1(4'b0000), .in2(4'b0000), .in3(4'b0101), .in4(4'b0000), .in5(4'b0000), .in6(4'b0000),
    .in7(4'b0000), .in8(4'b0000), .in9(4'b0000), .in10(4'b0000), .in11(4'b0101), .in12(4'b0000),
    .in13(4'b0000), .in14(4'b0000), .in15(4'b0000), .in16(4'b0000), .in17(4'b0000), .in18(4'b0000),
    .in19(4'b0000), .in20(4'b0000), .in21(4'b0000), .in22(4'b0000), .in23(4'b0000), .in24(4'b0000),
    .in25(4'b0000), .in26(4'b0000), .in27(4'b0000), .in28(4'b0000), .in29(4'b0000), .in30(4'b0000),
    .in31(4'b0000), .out(multiplexer_2_out), .sel(in_1[30:26]));
  Multiplexer #(.width(4), .enable("false")) multiplexer_3 (
    .in0(multiplexer_1_out), .in1(multiplexer_2_out), .out(multiplexer_3_out), .sel(in_1[31]));
  Multiplexer #(.width(4), .enable("false")) multiplexer_4 (
    .in0(funct_decider_1_out_2), .in1(multiplexer_3_out), .out(out_2), .sel(Type_Control));

  // Other names for the same wires on the sheet: Func[5:0] = in_1[5:0]; _5OB[4:0] = in_1[30:26]; _1OB = in_1[31]
endmodule

module Funct_Decider (
  input  [5:0] in_1,
  output [3:0] out_2
);

  wire [3:0] multiplexer_1_out, multiplexer_2_out, undriven;

  Multiplexer #(.select(5), .width(4), .disabled(0), .enable("false")) multiplexer_1 (
    .in0(4'b0000), .in1(undriven), .in2(4'b0001), .in3(4'b0000), .in4(4'b0000), .in5(4'b0000), .in6(4'b0000),
    .in7(4'b0000), .in8(4'b0101), .in9(4'b0000), .in10(4'b0000), .in11(4'b0000), .in12(4'b0000),
    .in13(4'b0000), .in14(4'b0000), .in15(4'b0000), .in16(4'b0000), .in17(4'b0000), .in18(4'b0000),
    .in19(4'b0000), .in20(4'b0000), .in21(4'b0000), .in22(4'b0000), .in23(4'b0000), .in24(4'b0000),
    .in25(4'b0000), .in26(4'b0000), .in27(4'b0000), .in28(4'b0000), .in29(4'b0000), .in30(4'b0000),
    .in31(4'b0000), .out(multiplexer_1_out), .sel(in_1[4:0]));
  Multiplexer #(.select(5), .width(4), .enable("false")) multiplexer_2 (
    .in0(4'b0011), .in1(4'b0101), .in2(4'b0000), .in3(4'b0000), .in4(4'b1000), .in5(4'b1001), .in6(4'b0000),
    .in7(4'b0000), .in8(4'b0000), .in9(4'b0000), .in10(4'b1011), .in11(4'b1100), .in12(4'b0000),
    .in13(4'b0000), .in14(4'b0000), .in15(4'b0000), .in16(4'b0000), .in17(4'b0000), .in18(4'b0000),
    .in19(4'b0000), .in20(4'b0000), .in21(4'b0000), .in22(4'b0000), .in23(4'b0000), .in24(4'b0000),
    .in25(4'b0000), .in26(4'b0000), .in27(4'b0000), .in28(4'b0000), .in29(4'b0000), .in30(4'b0000),
    .in31(4'b0000), .out(multiplexer_2_out), .sel(in_1[4:0]));
  Multiplexer #(.width(4), .enable("false")) multiplexer_3 (
    .in0(multiplexer_1_out), .in1(multiplexer_2_out), .out(out_2), .sel(in_1[5]));

  // Other names for the same wires on the sheet: _5B[4:0] = in_1[4:0]; _1B = in_1[5]
endmodule
