// Logisim project alu-3.circ as structural Verilog: 13 circuits, main circuit main
module main (
  input  [31:0] X,
  input  [31:0] Y,
  input  [3:0] Switch,
  output Signed_Overflow,
  output Equal,
  output [31:0] Result
);

  wire addover, subover;
  wire [31:0] add, addu, \and , \or , sll, slt, sltu, sra, srl, sub, subu, \xor ;

  sll u_sll (.Y(Y), .X(X), .out(sll));
  srl u_srl (.Y(Y), .X(X), .out(srl));
  sra u_sra (.Y(Y), .X(X), .out(sra));
  add u_add (.X(X), .Y(Y), .out(add), .signedOverflow(addover));
  Comparator #(.width(32)) comparator_1 (.a(X), .b(Y), .eq(Equal));  // open: gt, lt
  addu u_addu (.X(X), .Y(Y), .out(addu));
  sub u_sub (.X(X), .Y(Y), .out(sub), .signedOverflow(subover));
  subu u_subu (.X(X), .Y(Y), .out(subu));
  \and  u_and (.X(X), .Y(Y), .out(\and ));
  \or  u_or (.X(X), .Y(Y), .out(\or ));
  \xor  u_xor (.X(X), .Y(Y), .out(\xor ));
  slt u_slt (.X(X), .Y(Y), .out(slt));
  sltu u_sltu (.X(X), .Y(Y), .out(sltu));
  Multiplexer #(.select(4), .width(32), .enable("false")) multiplexer_1 (
    .in0(sll), .in1(srl), .in2(sra), .in3(add), .in4(addu), .in5(sub), .in6(subu), .in7(\and ), .in8(\or ),
    .in9(\xor ), .in10(slt), .in11(sltu), .out(Result), .sel(Switch));  // open: in12, in13, in14, in15
  Multiplexer #(.select(4), .disabled(0), .enable("false")) multiplexer_2 (
    .in0(1'b0), .in1(1'b0), .in2(1'b0), .in3(addover), .in4(1'b0), .in5(subover), .in6(1'b0), .in7(1'b0),
    .in8(1'b0), .in9(1'b0), .in10(1'b0), .in11(1'b0), .in12(1'b0), .in13(1'b0), .in14(1'b0), .in15(1'b0),
    .out(Signed_Overflow), .sel(Switch));

  // Other names for the same wires on the sheet: overflow = Signed_Overflow; S[3:0] = Switch

  // Notes on the sheet:
  //   INPUTS to your circuit
  //   DON'T CHANGE THE LOCATIONS OF THE INPUTS AND OUTPUTS!
  //   OUTPUTS from your circuit
endmodule

module sll (
  input  [31:0] Y,
  input  [31:0] X,
  output [31:0] out
);

  Shifter #(.width(32)) shifter_1 (.in(Y), .\dist (X[4:0]), .out(out));
endmodule

module srl (
  input  [31:0] Y,
  input  [31:0] X,
  output [31:0] out
);

  Shifter #(.width(32), .shift("lr")) shifter_1 (.in(Y), .\dist (X[4:0]), .out(out));
endmodule

module sra (
  input  [31:0] Y,
  input  [31:0] X,
  output [31:0] out
);

  Shifter #(.width(32), .shift("ar")) shifter_1 (.in(Y), .\dist (X[4:0]), .out(out));
endmodule

module add (
  input  [31:0] X,
  input  [31:0] Y,
  output [31:0] out,
  output signedOverflow
);

  wire and_1_out, nand_1_out;

  and and_1 (and_1_out, X[31], Y[31]);
  nand nand_1 (nand_1_out, X[31], Y[31]);
  Adder #(.width(32)) adder_1 (.a(X), .b(Y), .out(out));  // open: cin, cout
  or or_1 (signedOverflow, and_1_out, nand_1_out);
endmodule

module addu (
  input  [31:0] X,
  input  [31:0] Y,
  output [31:0] out
);

  Adder #(.width(32)) adder_1 (.a(X), .b(Y), .out(out));  // open: cin, cout
endmodule

module sub (
  input  [31:0] X,
  input  [31:0] Y,
  output [31:0] out,
  output signedOverflow
);

  Subtractor #(.width(32)) subtractor_1 (.a(X), .b(Y), .out(out));  // open: bin, bout
  xor xor_1 (signedOverflow, X[31], Y[31]);
endmodule

module subu (
  input  [31:0] X,
  input  [31:0] Y,
  output [31:0] out
);

  Subtractor #(.width(32)) subtractor_1 (.a(X), .b(Y), .out(out));  // open: bin, bout
endmodule

module \and  (
  input  [31:0] X,
  input  [31:0] Y,
  output [31:0] out
);

  assign out = X & Y;  // AND_Gate and_1, 32 bits wide
endmodule

module \or  (
  input  [31:0] X,
  input  [31:0] Y,
  output [31:0] out
);

  assign out = X | Y;  // OR_Gate or_1, 32 bits wide
endmodule

module \xor  (
  input  [31:0] X,
  input  [31:0] Y,
  output [31:0] out
);

  assign out = X ^ Y;  // XOR_Gate xor_1, 32 bits wide
endmodule

module slt (
  input  [31:0] X,
  input  [31:0] Y,
  output [31:0] out
);

  wire comparator_1_lt;

  Comparator #(.width(32)) comparator_1 (.a(X), .b(Y), .lt(comparator_1_lt));  // open: gt, eq
  assign out = {{31{1'b0}}, comparator_1_lt};  // Bit_Extender bit_extender_1
endmodule

module sltu (
  input  [31:0] X,
  input  [31:0] Y,
  output [31:0] out
);

  wire comparator_1_lt;

  Comparator #(.width(32), .mode("unsigned")) comparator_1 (.a(X), .b(Y), .lt(comparator_1_lt));  // open: gt, eq
  assign out = {{31{1'b0}}, comparator_1_lt};  // Bit_Extender bit_extender_1
endmodule
