// Logisim project cpu.circ as structural Verilog: 1 circuit, main circuit main
module main (
  input  [31:0] INSTRUCTION,
  input  CLOCK,
  input  [31:0] data,
  input  [31:0] address,
  output [31:0] FETCH_ADDRESS,
  output [31:0] s0_Value,
  output [31:0] s1_Value,
  output [31:0] s2_Value,
  output [31:0] ra_Value,
  output [31:0] sp_Value
);

  wire ALUSrc, and_1_out, branch, comparator_1_eq, comparator_1_gt, comparator_2_eq, comparator_2_lt, Jump,
       main_2_p1, main_2_p2, main_2_p4, main_2_p18, main_2_p19, main_3_equal, main_4_p1, main_4_p2,
       main_4_p7, MemtoReg, Memwrite, or_2_out, or_3_out, or_4_out, RegDst, RegWrite;
  wire [3:0] adder_1_out_2, ALUOp, register_1_q;
  wire [4:0] main_2_p7;
  wire [27:0] adder_1_out;
  wire [31:0] adder_2_out, bit_extender_1_out, bit_extender_2_out, bit_extender_3_out, main_2_p9, main_2_p16,
       main_2_p17, main_3_result, main_4_p9, multiplexer_1_out, multiplexer_2_out, multiplexer_4_out,
       or_1_out, shifter_1_out, shifter_2_out, shifter_3_out;
  wire [31:4] register_1_q_2;

  Multiplexer #(.width(32), .enable("false")) multiplexer_1 (
    .in0({adder_1_out_2, adder_1_out}), .in1(adder_2_out), .out(multiplexer_1_out), .sel(and_1_out));
  Register #(.width(32)) PC (.D(multiplexer_2_out), .Q(FETCH_ADDRESS), .clk(CLOCK));  // open: en, clr
  Multiplexer #(.width(32), .enable("false")) multiplexer_2 (
    .in0(multiplexer_1_out), .in1(or_1_out), .out(multiplexer_2_out), .sel(Jump));
  Adder #(.width(32)) adder_1 (.a(FETCH_ADDRESS), .b(32'h4), .out({adder_1_out_2, adder_1_out}));  // open: cin, cout
  assign or_1_out = shifter_1_out | shifter_2_out;  // OR_Gate or_1, 32 bits wide
  assign bit_extender_1_out = {{28{1'b0}}, adder_1_out_2};  // Bit_Extender bit_extender_1
  Shifter #(.width(32)) shifter_1 (.in(bit_extender_1_out), .\dist (5'b11100), .out(shifter_1_out));
  assign bit_extender_2_out = {{6{1'b0}}, INSTRUCTION[25:0]};  // Bit_Extender bit_extender_2
  Shifter #(.width(32)) shifter_2 (.in(bit_extender_2_out), .\dist (5'b00010), .out(shifter_2_out));
  Control_Unit_main main_1 (
    .Instruction(INSTRUCTION), .RegWrite(RegWrite), .RegDst(RegDst), .ALUSrc(ALUSrc), .Branch(branch),
    .Memwrite(Memwrite), .MemtoReg(MemtoReg), .ALUOp(ALUOp), .Jump(Jump));
  assign bit_extender_3_out = {{16{INSTRUCTION[15]}}, INSTRUCTION[15:0]};  // Bit_Extender bit_extender_3
  // regfile_main main_2: pin names not known; wires that end beside it: main_2_p1, main_2_p2, main_2_p2, main_2_p4, INSTRUCTION[25:21], INSTRUCTION[20:16], main_2_p7, data, main_2_p9, address, RegWrite, s2_Value, CLOCK, ra_Value, sp_Value, main_2_p16, main_2_p17, main_2_p18, main_2_p19, main_2_p19
  Multiplexer #(.width(5), .enable("false")) multiplexer_3 (
    .in0(INSTRUCTION[20:16]), .in1(INSTRUCTION[15:11]), .out(main_2_p7), .sel(RegDst));
  Multiplexer #(.width(32), .enable("false")) multiplexer_4 (
    .in0(main_2_p17), .in1(bit_extender_3_out), .out(multiplexer_4_out), .sel(ALUSrc));
  Comparator #(.width(32), .mode("unsigned")) comparator_1 (
    .a(address), .b(32'h7f00), .gt(comparator_1_gt), .eq(comparator_1_eq));  // open: lt
  alu_3_main main_3 (
    .Switch(ALUOp), .X(main_2_p16), .Equal(main_3_equal), .Result(main_3_result), .Y(multiplexer_4_out));  // open: Signed_Overflow
  Shifter #(.width(32)) shifter_3 (.in(bit_extender_3_out), .\dist (5'b00010), .out(shifter_3_out));
  Comparator #(.width(32), .mode("unsigned")) comparator_2 (
    .a(address), .b(32'h7f08), .eq(comparator_2_eq), .lt(comparator_2_lt));  // open: gt
  or or_2 (or_2_out, comparator_2_eq, comparator_2_lt);
  or or_3 (or_3_out, comparator_1_gt, comparator_1_eq);
  and and_1 (and_1_out, branch, main_3_equal);
  Adder #(.width(32)) adder_2 (
    .a(shifter_3_out), .b({adder_1_out_2, adder_1_out}), .out(adder_2_out));  // open: cin, cout
  or or_4 (or_4_out, or_2_out, or_3_out);
  Register #(.width(32)) register_1 (
    .D(data), .en(or_4_out), .Q({register_1_q_2, register_1_q}), .clk(CLOCK));  // open: clr
  // mem_main main_4: pin names not known; wires that end beside it: main_4_p1, main_4_p2, main_4_p2, main_3_result, main_2_p17, Memwrite, main_4_p7, CLOCK, main_4_p9, main_4_p7, main_2_p18
  Hex_Digit_Display hex_digit_display_1 (.value(register_1_q));  // open: dp
  Multiplexer #(.width(32), .enable("false")) multiplexer_5 (
    .in0(main_3_result), .in1(main_4_p9), .out(main_2_p9), .sel(MemtoReg));

  assign s0_Value = data;
  assign s1_Value = address;

  // Other names for the same wires on the sheet: clk = CLOCK; fetch_addr[31:0] = FETCH_ADDRESS; ra[31:0] = ra_Value;
  //   s0[31:0] = data; s1[31:0] = address; s2[31:0] = s2_Value; sp[31:0] = sp_Value

  // Notes on the sheet:
  //   Output
  //   These are outputs/inputs from run.circ
  //   Inputs
  //   These are DEBUG/TEST outputs from your circuit.
endmodule
