// Logisim project CPU-starter_kit_test copy 2.circ as structural Verilog: 1 circuit, main circuit main
module main (
  output [31:0] s0_Value,
  output [31:0] s1_Value,
  output [31:0] s2_Value,
  output [31:0] sp_Value,
  output [31:0] out_5,
  output halt
);

  wire clock_1_out, main_1_p6;
  wire [31:0] counter_1_q, fetch_addr;

  Clock clock_1 (.out(clock_1_out));
  // cpu_main main_1: pin names not known; wires that end beside it: out_5, s0_Value, s1_Value, clock_1_out, s2_Value, main_1_p6, sp_Value, fetch_addr
  Counter #(.width(32), .max('hffffffff)) counter_1 (
    .Q(counter_1_q), .clk(clock_1_out));  // open: load, D, count, carry, clr
  Comparator #(.width(32)) comparator_1 (.a(counter_1_q), .b(32'h10), .eq(halt));  // open: gt, lt
  // Probe on fetch_addr
  ROM #(.addrWidth(24), .dataWidth(32)) rom_1 (.addr(fetch_addr[25:2]), .data(out_5));  // open: sel
  // Probe on out_5

  // Other names for the same wires on the sheet: Instruction[31:0] = out_5

  // Notes on the sheet:
  //   YOUR CPU SHOULD FIT IN HERE!
  //   Instruction Memory
  //   contents of rom_1 (hex, n*v repeats v):
  //   20100004 108080 20110010 118842
endmodule
